# Fritzing sketch ReadAnalogVoltage (saved by Fritzing 0.8.5b)
breadboards: 1

parts:
  Componente1 = Arduino Uno (Rev3)
  R1 = Rotary Potentiometer (Small) [maximum_resistance=100kΩ package=THT]
  LED1 = LED - 5mm [color="Red (633nm)" package="5 mm [THT]"]
  LED2 = LED - 5mm [color="Blue (470nm)" package="5 mm [THT]"]
  LED3 = LED - 5mm [color="White (6500K)" package="5 mm [THT]"]

nets:
  N1: Componente1.A1, R1.wiper
  N2: Componente1.D9_PWM, LED2.anode
  N3: Componente1.D10_PWM/SS, LED3.anode
  N4: Componente1.D11_PWM/MOSI, LED1.anode
  N5: Componente1.GND, LED1.cathode, LED2.cathode, LED3.cathode
  N6: Componente1.5V, R1.leg1
