# Fritzing sketch LedControl (saved by Fritzing 0.8.5b)
circuit board: 8.46667cm x 5.64444cm
breadboards: 1

parts:
  Componente1 = Arduino Uno (Rev3) [part_number=1]
  S1 = Pushbutton [part_number=1 package="[THT]"]
  R1 = Resistor [tolerance=±5% resistance=10k part_number=2 package=THT]
  LED1 = LED - 5mm [color="Blue (430nm)" part_number=1 package="5 mm [THT]"]
  R2 = Rotary Potentiometer (Small) [maximum_resistance=100kΩ part_number=3 package=THT]
  R3 = Resistor [tolerance=±5% resistance=220 part_number=1 package=THT]
  LED2 = LED - 5mm [color="Red (633nm)" package="5 mm [THT]"]

nets:
  N1: Componente1.A0, R2.wiper
  N2: Componente1.GND, R1.Pin_1, LED1.cathode, R2.leg1, LED2.cathode
  N3: Componente1.D2, S1.Pin_1, S1.Pin_2, R1.Pin_0
  N4: Componente1.D3_PWM, R3.Pin_1
  N5: Componente1.D4, LED2.anode
  N6: Componente1.5V, S1.Pin_3, S1.Pin_4, R2.leg2
  N7: LED1.anode, R3.Pin_0
